// Logisim project SmartWaterTank_Martins_Ngene.circ as structural Verilog: 9 circuits, main circuit main
module main (
  input  S0,
  input  S1,
  input  S2,
  input  S3,
  input  RESET
);

  wire _1__Sensor_Encoder_fault, _1__Sensor_Encoder_l0, _1__Sensor_Encoder_l1, _1__Sensor_Encoder_valid,
       _2__Full_Comparator_full, _3__Pump_Control_pump, _4__Level_Register_r0, _4__Level_Register_r1,
       _5__Overflow_Counter_alarm, _5__Overflow_Counter_q0, _5__Overflow_Counter_q1, _6a__2_bit_to_BCD_a,
       _6a__2_bit_to_BCD_b, _6a__2_bit_to_BCD_c, _6a__2_bit_to_BCD_d, CLK_out, Level_Status_full,
       Level_Status_low, Level_Status_medium, sa, sb, sc, sd, se, sf, sg;

  Clock CLK (.out(CLK_out));
  ENCODER _1__Sensor_Encoder (
    .S0(S0), .S1(S1), .S2(S2), .S3(S3), .L1(_1__Sensor_Encoder_l1), .L0(_1__Sensor_Encoder_l0),
    .VALID(_1__Sensor_Encoder_valid), .FAULT(_1__Sensor_Encoder_fault));
  COMPARATOR _2__Full_Comparator (
    .A1(_1__Sensor_Encoder_l1), .A0(_1__Sensor_Encoder_l0), .FULL(_2__Full_Comparator_full));
  PUMP_CTRL _3__Pump_Control (.L1(_1__Sensor_Encoder_l1), .L0(_1__Sensor_Encoder_l0), .PUMP(_3__Pump_Control_pump));
  LEVEL_REG _4__Level_Register (
    .L1(_1__Sensor_Encoder_l1), .L0(_1__Sensor_Encoder_l0), .LOAD(_1__Sensor_Encoder_valid), .CLK(CLK_out),
    .RESET(RESET), .R1(_4__Level_Register_r1), .R0(_4__Level_Register_r0));
  BIN_TO_BCD _6a__2_bit_to_BCD (
    .L1(_4__Level_Register_r1), .L0(_4__Level_Register_r0), .D(_6a__2_bit_to_BCD_d), .C(_6a__2_bit_to_BCD_c),
    .B(_6a__2_bit_to_BCD_b), .A(_6a__2_bit_to_BCD_a));
  STATUS Level_Status (
    .R1(_4__Level_Register_r1), .R0(_4__Level_Register_r0), .LOW(Level_Status_low),
    .MEDIUM(Level_Status_medium), .FULL(Level_Status_full));
  COUNTER _5__Overflow_Counter (
    .FULL(_2__Full_Comparator_full), .CLK(CLK_out), .RESET(RESET), .Q1(_5__Overflow_Counter_q1),
    .Q0(_5__Overflow_Counter_q0), .ALARM(_5__Overflow_Counter_alarm));
  LED PUMP_ON (.in(_3__Pump_Control_pump));
  LED FULL_DETECT (.in(_2__Full_Comparator_full));
  LED ALARM (.in(_5__Overflow_Counter_alarm));
  LED SENSOR_FAULT (.in(_1__Sensor_Encoder_fault));
  LED LOW (.in(Level_Status_low));
  LED MEDIUM (.in(Level_Status_medium));
  LED FULL (.in(Level_Status_full));
  LED CNT_Q1 (.in(_5__Overflow_Counter_q1));
  LED CNT_Q0 (.in(_5__Overflow_Counter_q0));
  _7_Segment_Display u_7_segment_display_1 (.g(sg), .f(sf), .a(sa), .b(sb), .e(se), .d(sd), .c(sc));  // open: dp
  BCD_7SEG _6b__BCD_7seg_Decoder (
    .D(_6a__2_bit_to_BCD_d), .C(_6a__2_bit_to_BCD_c), .B(_6a__2_bit_to_BCD_b), .A(_6a__2_bit_to_BCD_a),
    .seg_a(sa), .seg_b(sb), .seg_c(sc), .seg_d(sd), .seg_e(se), .seg_f(sf), .seg_g(sg));

  // Notes on the sheet:
  //   Martins Ngene 200 Level Computer Science - IFT 211 Lab Assessment
endmodule

module ENCODER (
  input  S0,
  input  S1,
  input  S2,
  input  S3,
  output L1,
  output L0,
  output VALID,
  output FAULT
);

  wire and_1_out, and_2_out, and_3_out, and_4_out, not_1_out, not_2_out, not_3_out;

  not not_1 (not_1_out, S0);
  not not_2 (not_2_out, S1);
  not not_3 (not_3_out, S2);
  or or_1 (L1, S3, S2);
  and and_1 (and_1_out, S1, not_3_out);
  and and_2 (and_2_out, S3, not_3_out);
  and and_3 (and_3_out, S2, not_2_out);
  and and_4 (and_4_out, S1, not_1_out);
  or or_2 (L0, S3, and_1_out);
  or or_3 (FAULT, and_2_out, and_3_out, and_4_out);
  not not_4 (VALID, FAULT);
endmodule

module COMPARATOR (
  input  A1,
  input  A0,
  output FULL
);

  wire xnor_1_out, xnor_2_out;

  xnor xnor_1 (xnor_1_out, A1, 1'b1);
  xnor xnor_2 (xnor_2_out, A0, 1'b1);
  and and_1 (FULL, xnor_1_out, xnor_2_out);
endmodule

module PUMP_CTRL (
  input  L1,
  input  L0,
  output PUMP
);

  nand nand_1 (PUMP, L1, L0);
endmodule

module LEVEL_REG (
  input  L1,
  input  L0,
  input  LOAD,
  input  CLK,
  input  RESET,
  output R1,
  output R0
);

  wire and_1_out, and_2_out, and_3_out, and_4_out, not_1_out, or_1_out, or_2_out;

  not not_1 (not_1_out, LOAD);
  and and_1 (and_1_out, LOAD, L1);
  and and_2 (and_2_out, LOAD, L0);
  and and_3 (and_3_out, not_1_out, R1);
  and and_4 (and_4_out, not_1_out, R0);
  or or_1 (or_1_out, and_1_out, and_3_out);
  or or_2 (or_2_out, and_2_out, and_4_out);
  D_Flip_Flop FF1 (.D(or_1_out), .clk(CLK), .Q(R1), .reset(RESET));  // open: Qn, preset
  D_Flip_Flop FF0 (.D(or_2_out), .clk(CLK), .Q(R0), .reset(RESET));  // open: Qn, preset

  // Other names for the same wires on the sheet: Q0 = R0; Q1 = R1
endmodule

module COUNTER (
  input  FULL,
  input  CLK,
  input  RESET,
  output Q1,
  output Q0,
  output ALARM
);

  wire and_2_out, and_3_out, not_1_out, or_1_out, or_2_out;

  not not_1 (not_1_out, Q0);
  or or_1 (or_1_out, Q1, Q0);
  and and_1 (ALARM, Q1, Q0);
  or or_2 (or_2_out, not_1_out, Q1);
  and and_2 (and_2_out, FULL, or_1_out);
  and and_3 (and_3_out, FULL, or_2_out);
  D_Flip_Flop C1 (.D(and_2_out), .clk(CLK), .Q(Q1), .reset(RESET));  // open: Qn, preset
  D_Flip_Flop C0 (.D(and_3_out), .clk(CLK), .Q(Q0), .reset(RESET));  // open: Qn, preset
endmodule

module BIN_TO_BCD (
  input  L1,
  input  L0,
  output D,
  output C,
  output B,
  output A
);


  assign A = L0;
  assign B = L1;
  assign C = 1'b0;
  assign D = 1'b0;
endmodule

module BCD_7SEG (
  input  D,
  input  C,
  input  B,
  input  A,
  output seg_a,
  output seg_b,
  output seg_c,
  output seg_d,
  output seg_e,
  output seg_f,
  output seg_g
);

  wire and_1_out, and_2_out, and_3_out, and_4_out, and_5_out, and_6_out, and_7_out, and_8_out, and_9_out,
       not_1_out, not_2_out, not_3_out, or_4_out;

  not not_1 (not_1_out, C);
  not not_2 (not_2_out, B);
  not not_3 (not_3_out, A);
  and and_1 (and_1_out, C, A);
  and and_2 (and_2_out, B, A);
  and and_3 (and_3_out, not_1_out, not_3_out);
  and and_4 (and_4_out, not_2_out, not_3_out);
  and and_5 (and_5_out, not_1_out, B);
  and and_6 (and_6_out, B, not_3_out);
  and and_7 (and_7_out, C, not_2_out, A);
  and and_8 (and_8_out, C, not_2_out);
  and and_9 (and_9_out, C, not_3_out);
  or or_1 (seg_c, C, not_2_out, A);
  or or_2 (seg_a, D, B, and_1_out, and_3_out);
  or or_3 (seg_b, not_1_out, and_4_out, and_2_out);
  or or_4 (or_4_out, D, and_3_out, and_5_out);
  or or_5 (seg_e, and_3_out, and_6_out);
  or or_6 (seg_f, D, and_4_out, and_8_out, and_9_out);
  or or_7 (seg_g, D, and_8_out, and_5_out, and_6_out);
  or or_8 (seg_d, or_4_out, and_6_out, and_7_out);
endmodule

module STATUS (
  input  R1,
  input  R0,
  output LOW,
  output MEDIUM,
  output FULL
);

  wire not_2_out;

  not not_1 (LOW, R1);
  not not_2 (not_2_out, R0);
  and and_1 (FULL, R1, R0);
  and and_2 (MEDIUM, R1, not_2_out);
endmodule
